# Fritzing sketch Waterdrops (saved by Fritzing 0.9.9b)
breadboards: 1

parts:
  Part1 = Arduino Ethernet Shield (Rev3)
  L1 = Solenoid
  Q1 = Basic FET N-Channel [package="D2Pak [SMD]"]
  Q2 = Basic FET N-Channel [package="D2Pak [SMD]"]
  L3 = Solenoid
  L4 = Solenoid
  Q3 = Basic FET N-Channel [package="D2Pak [SMD]"]
  L5 = Solenoid
  Q4 = Basic FET N-Channel [package="D2Pak [SMD]"]
  L6 = Solenoid
  Q5 = Basic FET N-Channel [package="D2Pak [SMD]"]
  Q6 = Basic FET N-Channel [package="D2Pak [SMD]"]
  Q7 = Basic FET N-Channel [package="D2Pak [SMD]"]
  Q8 = Basic FET N-Channel [package="D2Pak [SMD]"]
  Q9 = Basic FET N-Channel [package="D2Pak [SMD]"]
  L7 = Solenoid
  L8 = Solenoid
  L9 = Solenoid
  L10 = Solenoid
  L11 = Solenoid

nets:
  N1: Part1.GND, L1.pin2, Q1.source, Q2.source, L3.pin2, L4.pin2, Q3.source, L5.pin2, Q4.source, L6.pin2, Q5.source, Q6.source, Q7.source, Q8.source, Q9.source, L7.pin2, L8.pin2, L9.pin2, L10.pin2, L11.pin2
  N2: L1.pin1, Q1.drain, Q2.drain, L3.pin1, L4.pin1, Q3.drain, L5.pin1, Q4.drain, L6.pin1, Q5.drain, Q6.drain, Q7.drain, Q8.drain, Q9.drain, L7.pin1, L8.pin1, L9.pin1, L10.pin1, L11.pin1
